# Fritzing sketch 2019-11-15_LCD_1604 (saved by Fritzing 0.9.4)

parts:
  Raspberry_Pi_1 = Raspberry Pi 3 [part_number=RPI-3-V1.2]
  LCD2 = LCD I2C 1602

nets:
  N1: Raspberry_Pi_1.GPIO2, LCD2.SDA
  N2: Raspberry_Pi_1.GPIO3, LCD2.SCL
  GND: Raspberry_Pi_1.GND, LCD2.GND
  5V: Raspberry_Pi_1.5V, LCD2.VCC

custom parts:
  LCD I2C 1602: A standard character display, usually with 2x16 characters. Comes in many colors.
