# Fritzing sketch 2019-11-17_rasp_MCP3_MQ2_MQ3_MQ9 (saved by Fritzing 0.9.4)
breadboards: 1

parts:
  MCP1 = MCP3208
  Raspberry_Pi_1 = Raspberry Pi 3 [part_number=RPI-3-V1.2]
  Sensor1 = Gas Sensor Breakout Board
  Sensor2 = Gas Sensor Breakout Board
  Sensor3 = Gas Sensor Breakout Board

nets:
  N1: MCP1.Chan_0, Sensor1.AOUT
  N2: MCP1.Chan_1, Sensor2.AOUT
  N3: MCP1.Chan_2, Sensor3.AOUT
  GND: MCP1.DGND, MCP1.AGND, Raspberry_Pi_1.GND, Sensor1.GND, Sensor2.GND, Sensor3.GND
  N4: MCP1.CS/SHDN, Raspberry_Pi_1.GPIO8
  N5: MCP1.DIN, Raspberry_Pi_1.GPIO10
  N6: MCP1.DOUT, Raspberry_Pi_1.GPIO9
  N7: MCP1.CLK, Raspberry_Pi_1.GPIO11
  5V: MCP1.VREF, MCP1.VDD, Raspberry_Pi_1.5V, Sensor1.5V, Sensor2.5V, Sensor3.5V

custom parts:
  Gas Sensor Breakout Board: Gas sensor breakout board. Input voltage is 5V. Sensor output is available in analog and digital.
