# Fritzing sketch 2019-11-22_rasp_MCP3_mosture (saved by Fritzing 0.9.4)
breadboards: 1

parts:
  MCP1 = MCP3208
  Raspberry_Pi_1 = Raspberry Pi 3 [part_number=RPI-3-V1.2]
  元件2 = FC-28 Soil Hygrometer Module
  元件3 = FC-28 Soil Hygrometer Module - Probe

nets:
  N1: MCP1.Chan_0, 元件2.AO
  GND: MCP1.DGND, MCP1.AGND, Raspberry_Pi_1.GND, 元件2.GND
  N2: MCP1.CS/SHDN, Raspberry_Pi_1.GPIO8
  N3: MCP1.DIN, Raspberry_Pi_1.GPIO10
  N4: MCP1.DOUT, Raspberry_Pi_1.GPIO9
  N5: MCP1.CLK, Raspberry_Pi_1.GPIO11
  VDD: MCP1.VREF, MCP1.VDD, Raspberry_Pi_1.5V, 元件2.VCC
  N6: 元件2.POS, 元件3.POS
  N7: 元件2.NEG, 元件3.NEG

custom parts:
  FC-28 Soil Hygrometer Module: The FC-28 is a soil hygrometer module that uses the Texas Instruments LM393 comparator chip to provide an analog measurement of soil humidity. The digital output is high when soil moisture is over a certain threshold, as determined by adjusting the potentiometer.
  FC-28 Soil Hygrometer Module - Probe: The FC-28 is a soil hygrometer module that uses the Texas Instruments LM393 comparator chip to provide an analog measurement of soil humidity.
