# Fritzing sketch 2019-11-23_Matrix_Led_Modul (saved by Fritzing 0.9.3b)

parts:
  Raspberry_Pi_1 = Raspberry Pi 3 [part_number=RPI-3-V1.2]
  8x8_LED_Modul_mit_MAX1 = 8x8 LED Modul mit MAX7219 [package=THT]

nets:
  N1: Raspberry_Pi_1.GIPO10, 8x8_LED_Modul_mit_MAX1.DIN_Eingang
  N2: Raspberry_Pi_1.GIPO11, 8x8_LED_Modul_mit_MAX1.CLK_Eingang
  N3: Raspberry_Pi_1.GIPO8, 8x8_LED_Modul_mit_MAX1.CS_Eingang
  N4: Raspberry_Pi_1.GND, 8x8_LED_Modul_mit_MAX1.GND_Eingang
  N5: Raspberry_Pi_1.5V, 8x8_LED_Modul_mit_MAX1.VCC_Eingang
