# Fritzing sketch 2019-11-25_LCD_1604 (saved by Fritzing 0.9.4)

parts:
  LCD2 = LCD I2C 1602
  元件1 = Arduino Nano (Rev3.0)

nets:
  GND: LCD2.GND, 元件1.GND
  VCC: LCD2.VCC, 元件1.5V
  N1: LCD2.SDA, 元件1.A4
  N2: LCD2.SCL, 元件1.A5

custom parts:
  LCD I2C 1602: A standard character display, usually with 2x16 characters. Comes in many colors.
