# Fritzing sketch 2019-11-26-Arduino_7dig (saved by Fritzing 0.9.4)
breadboards: 1

parts:
  元件1 = Arduino Nano (Rev3.0)
  U1 = 74HC595 SMD [package="SO16 [SMD]"]
  7_Segment_4_Digit_Display1 = 7-SEGMENT-4DIGIT common anode [part_number="5461BS - 5462BS" package=7-segment-4digit-anode]

nets:
  N1: 元件1.D4, U1.SH_CP
  N2: 元件1.D5, U1.ST_CP
  N3: 元件1.D6, U1.DS
  N4: 元件1.D8, 7_Segment_4_Digit_Display1.pin_6
  N5: 元件1.D9, 7_Segment_4_Digit_Display1.pin_8
  N6: 元件1.D10, 7_Segment_4_Digit_Display1.pin_9
  N7: 元件1.D11/MOSI, 7_Segment_4_Digit_Display1.pin_12
  GND: 元件1.GND, U1.GND, U1.OE
  5V: 元件1.5V, U1.MR, U1.VCC
  N8: U1.Q1, 7_Segment_4_Digit_Display1.pin_7
  N9: U1.Q2, 7_Segment_4_Digit_Display1.pin_4
  N10: U1.Q3, 7_Segment_4_Digit_Display1.pin_2
  N11: U1.Q4, 7_Segment_4_Digit_Display1.pin_1
  N12: U1.Q5, 7_Segment_4_Digit_Display1.pin_10
  N13: U1.Q6, 7_Segment_4_Digit_Display1.pin_5
  N14: U1.Q7, 7_Segment_4_Digit_Display1.pin_3
  N15: U1.Q0, 7_Segment_4_Digit_Display1.pin_11

custom parts:
  7-SEGMENT-4DIGIT common anode: A 7 Segment 4 Digit common anode display, with decimal points
