# Fritzing sketch 2019-11-27_Arduino_MQ2_MQ3_MQ9 (saved by Fritzing 0.9.4)

parts:
  Sensor1 = Gas Sensor Breakout Board
  Sensor2 = Gas Sensor Breakout Board
  Sensor3 = Gas Sensor Breakout Board
  元件1 = Arduino Nano (Rev3.0)

nets:
  GND: Sensor1.GND, Sensor2.GND, Sensor3.GND, 元件1.GND
  N1: Sensor1.AOUT, 元件1.A3
  5V: Sensor1.5V, Sensor2.5V, Sensor3.5V, 元件1.5V
  N2: Sensor2.AOUT, 元件1.A2
  N3: Sensor3.AOUT, 元件1.A1

notes:
  MQ2
  MQ3
  MQ9

custom parts:
  Gas Sensor Breakout Board: Gas sensor breakout board. Input voltage is 5V. Sensor output is available in analog and digital.
