# Fritzing sketch 2019-11-28_Arduino_Lora (saved by Fritzing 0.9.4)

parts:
  J1 = Camdenboss CTB0158-4 [part_number=CTB0158-4 package=THT]
  元件1 = Arduino Nano (Rev3.0)
  元件2 = DHT22 module

nets:
  N1: J1.terminal_1, 元件1.AREF, 元件1.3V3
  N2: J1.terminal_2, 元件1.D10
  N3: J1.terminal_3, 元件1.D11/MOSI
  GND: J1.terminal_4, 元件1.GND, 元件2.GND
  N4: 元件1.D3, 元件2.DATA
  5V: 元件1.5V, 元件2.VCC

notes:
  3V3
  TXD
  RXD
  GND
  Lora models
