# Fritzing sketch 2019-12-03-Arduino_Bluetooth (saved by Fritzing 0.9.4)

parts:
  元件1 = Bluetooth HC-05 Macho
  元件2 = Arduino Nano (Rev3.0)

nets:
  N1: 元件1.TXD, 元件2.D8
  N2: 元件1.RXD, 元件2.D9
  VCC: 元件1.VCC, 元件2.5V, 元件2.A7
  GND: 元件1.GND, 元件2.GND
