# Fritzing sketch 2019-12-05-Raspberry_GPS (saved by Fritzing 0.9.4)

parts:
  元件1 = u-blox NEO-6M GPS Breakout
  Raspberry_Pi_1 = Raspberry Pi 3 [part_number=RPI-3-V1.2]

nets:
  GND: 元件1.GND, Raspberry_Pi_1.GND
  VCC: 元件1.VCC, Raspberry_Pi_1.5V
  N1: 元件1.TXD, Raspberry_Pi_1.GPIO15
  N2: 元件1.RXD, Raspberry_Pi_1.GPIO14
