# Fritzing sketch 2019-12-06-Arduino_GPS (saved by Fritzing 0.9.4)

parts:
  Raspberry_Pi_1 = Raspberry Pi 3 [part_number=RPI-3-V1.2]
  元件2 = Arduino Nano (Rev3.0)

nets:
  GND: Raspberry_Pi_1.GND, 元件2.GND
  N1: Raspberry_Pi_1.GPIO15, 元件2.D8
  N2: Raspberry_Pi_1.GPIO14, 元件2.D9
  5V: Raspberry_Pi_1.5V, 元件2.5V
