# Fritzing sketch 2019-12-07_Matrix_Led_Modul (saved by Fritzing 0.9.4)

parts:
  8x8_LED_Modul_mit_MAX1 = 8x8 LED Modul mit MAX7219 [package=THT]
  元件1 = Arduino Nano (Rev3.0)

nets:
  N1: 8x8_LED_Modul_mit_MAX1.VCC_Eingang, 元件1.5V
  N2: 8x8_LED_Modul_mit_MAX1.GND_Eingang, 元件1.GND
  N3: 8x8_LED_Modul_mit_MAX1.DIN_Eingang, 元件1.D12/MISO
  N4: 8x8_LED_Modul_mit_MAX1.CS_Eingang, 元件1.D10
  N5: 8x8_LED_Modul_mit_MAX1.CLK_Eingang, 元件1.D11/MOSI
