# Fritzing sketch 2019-12-08-PMS5003_and_LCD1604 (saved by Fritzing 0.9.4)

parts:
  J1 = double row female pin header, 8 pins [form="♀ (female)"]
  LCD1 = LCD I2C 1602
  元件1 = Arduino Uno (Rev3)

nets:
  N1: J1.pin1, LCD1.VCC
  N2: J1.pin2, 元件1.GND
  N3: J1.pin5, 元件1.D11_PWM/MOSI
  N4: LCD1.SDA, 元件1.A4/SDA
  N5: LCD1.SCL, 元件1.A5/SCL

notes:
  PMS5003
  TXD

custom parts:
  LCD I2C 1602: A standard character display, usually with 2x16 characters. Comes in many colors.
