# Fritzing sketch 2019-12-09_Arduino_mosture (saved by Fritzing 0.9.4)

parts:
  元件2 = FC-28 Soil Hygrometer Module
  元件3 = FC-28 Soil Hygrometer Module - Probe
  元件4 = Arduino Nano (Rev3.0)

nets:
  VCC: 元件2.VCC, 元件4.5V
  GND: 元件2.GND, 元件4.GND
  N1: 元件2.AO, 元件4.A3
  N2: 元件2.POS, 元件3.POS
  N3: 元件2.NEG, 元件3.NEG

custom parts:
  FC-28 Soil Hygrometer Module: The FC-28 is a soil hygrometer module that uses the Texas Instruments LM393 comparator chip to provide an analog measurement of soil humidity. The digital output is high when soil moisture is over a certain threshold, as determined by adjusting the potentiometer.
  FC-28 Soil Hygrometer Module - Probe: The FC-28 is a soil hygrometer module that uses the Texas Instruments LM393 comparator chip to provide an analog measurement of soil humidity.
