# Fritzing sketch 2019-12-15_relay (saved by Fritzing 0.9.4)

parts:
  元件1 = HC-SR501 Body Sensor Module
  KY-1 = Keyes Relay [package=THT]
  VCC1 = 4 x AAA Battery Mount
  LED1 = LED - 5mm [color="Red (633nm)" package="5 mm [THT]"]

nets:
  N1: 元件1.VCC, KY-1.power, VCC1.+, LED1.anode
  N2: 元件1.GND, KY-1.ground, VCC1.-
  N3: KY-1.NO, LED1.cathode

custom parts:
  HC-SR501 Body Sensor Module: Pyroelectric Infrared PIR Motion Sensor Detector Module
  Keyes Relay: The Keyes 5V relay module is suitable for SCM development, home appliance control. It uses a 5V~12V TIL control signal which can control DC / AC signal.
